# Fritzing sketch vr_headset_wiring (saved by Fritzing 0.9.5d)

parts:
  Rotation_Tracking = Arduino Uno (Rev3)
  BNO055 = Grove 3 Axis Digital Accelerometer 16g

nets:
  N1: Rotation_Tracking.A4/SDA, BNO055.SDA
  N2: Rotation_Tracking.A5/SCL, BNO055.SCL
  GND: Rotation_Tracking.GND, BNO055.GND
  5V: Rotation_Tracking.5V, BNO055.VCC
